# Fritzing sketch pcbArduinoPart (saved by Fritzing 0.8.7b)
circuit board: 2.88315cm x 5.25564cm
breadboards: 1

parts:
  J1 = female pin header, 4 pins [form="♀ (female)"]
  J2 = female pin header, 6 pins [form="♀ (female)"]
  J3 = female pin header, 3 pins [form="♀ (female)"]
  tip121 = Voltage Regulator - 5V [package="TO220 [THT]"]
  27ohm = Resistor [tolerance=±5% resistance=2.2k package=THT]
  2_2K = Resistor [tolerance=±5% resistance=2.2k package=THT]
  J5 = female pin header, 2 pins [form="♀ (female)"]
  J6 = female pin header, 4 pins [form="♀ (female)"]
  AnalogPins = female pin header, 4 pins [form="♀ (female)"]  # not connected

nets:
  N1: J1.pin4, 2_2K.Pin_1, J6.pin3
  N2: J2.pin1, J6.pin1
  N3: J2.pin2, J6.pin2
  N4: J3.pin2, 27ohm.Pin_0
  N5: tip121.input_voltage, 27ohm.Pin_1
  N6: tip121.GND, J5.pin2
  N7: 2_2K.Pin_0, J5.pin1

notes:
  sensors
  GND
  Wishing Wall
  Varvara & Mar
