# Fritzing sketch pcbBoard (saved by Fritzing 0.8.7b)
circuit board: 6.42056cm x 6.39702cm
breadboards: 1

parts:
  LED1 = LED - 5mm [color="Red (633nm)" package="5 mm [THT]"]
  R = LED - 5mm [color="Red (633nm)" package="5 mm [THT]"]
  LED3 = LED - 5mm [color="Red (633nm)" package="5 mm [THT]"]
  J1 = female pin header, 3 pins [form="♀ (female)"]
  C1 = Electrolytic Capacitor [capacitance=10µF voltage=35V package="100 mil [THT, electrolytic]"]
  C2 = Electrolytic Capacitor [capacitance=10µF voltage=35V package="100 mil [THT, electrolytic]"]
  sensor1 = female pin header, 3 pins [form="♀ (female)"]
  J4 = female pin header, 2 pins [form="♀ (female)"]
  J3 = female pin header, 5 pins [form="♀ (female)"]

nets:
  N1: LED1.cathode, LED3.cathode, J4.pin2
  N2: LED1.anode, R.anode, LED3.anode, J4.pin1
  N3: R.cathode, J3.pin4
  N4: J1.pin1, J3.pin5
  N5: J1.pin2, C1.+
  N6: C2.+, sensor1.pin2, J3.pin1
  N7: sensor1.pin3, J3.pin2

notes:
  sig
  LED
